// Logisim project NAND_GATE_7400.circ as structural Verilog: 1 circuit, main circuit main
// A
module main (
  input  C,
  input  in_2
);

  wire dipswitch_1_sw1, dipswitch_1_sw8, n7400_1_p4, nand_1_out;

  DipSwitch dipswitch_1 (.sw1(dipswitch_1_sw1), .sw8(dipswitch_1_sw8));  // open: sw2, sw3, sw4, sw5, sw6, sw7
  // _7400 7400_1: pin names not known; wires that end beside it: 1'b1, dipswitch_1_sw1, dipswitch_1_sw8, n7400_1_p4, 1'b0
  LED led_1 (.in(n7400_1_p4));
  nand nand_1 (nand_1_out, C, in_2);
  LED X (.in(nand_1_out));

  // Notes on the sheet:
  //   A
  //   Inputs
  //   B
  //   X
  //   Output LED
endmodule
