// Logisim project Universality_of_NAND_GATE.circ as structural Verilog: 1 circuit, main circuit main
module main (
);

  wire dipswitch_1_sw1, dipswitch_1_sw4, dipswitch_1_sw5, dipswitch_1_sw7, dipswitch_1_sw8, dipswitch_2_sw1,
       dipswitch_2_sw4, dipswitch_2_sw5, dipswitch_2_sw7, dipswitch_2_sw8, n7400_1_pin3, n7400_1_pin6,
       n7400_1_pin8, n7400_2_pin1, n7400_2_pin2, n7400_2_pin3, nand_1_out, nand_2_out, nand_3_out,
       nand_4_out, nand_5_out, nand_6_out;

  DipSwitch dipswitch_1 (
    .sw1(dipswitch_1_sw1), .sw4(dipswitch_1_sw4), .sw5(dipswitch_1_sw5), .sw7(dipswitch_1_sw7),
    .sw8(dipswitch_1_sw8));  // open: sw2, sw3, sw6
  nand nand_1 (nand_1_out, dipswitch_1_sw1, dipswitch_1_sw1);
  nand nand_2 (nand_2_out, dipswitch_1_sw4, dipswitch_1_sw5);
  nand nand_3 (nand_3_out, dipswitch_1_sw7, dipswitch_1_sw7);
  nand nand_4 (nand_4_out, dipswitch_1_sw8, dipswitch_1_sw8);
  LED led_1 (.in(nand_1_out));
  nand nand_5 (nand_5_out, nand_2_out, nand_2_out);
  nand nand_6 (nand_6_out, nand_3_out, nand_4_out);
  LED led_2 (.in(nand_5_out));
  LED led_3 (.in(nand_6_out));
  DipSwitch dipswitch_2 (
    .sw1(dipswitch_2_sw1), .sw4(dipswitch_2_sw4), .sw5(dipswitch_2_sw5), .sw7(dipswitch_2_sw7),
    .sw8(dipswitch_2_sw8));  // open: sw2, sw3, sw6
  _7400 u_7400_1 (
    .pin1(dipswitch_2_sw1), .pin2(dipswitch_2_sw1), .pin3(n7400_1_pin3), .pin4(dipswitch_2_sw5),
    .pin5(dipswitch_2_sw4), .pin6(n7400_1_pin6), .pin10(n7400_1_pin6), .pin9(n7400_1_pin6),
    .pin8(n7400_1_pin8));  // open: pin13, pin12, pin11
  LED led_4 (.in(n7400_1_pin3));
  _7400 u_7400_2 (
    .pin1(n7400_2_pin1), .pin2(n7400_2_pin2), .pin3(n7400_2_pin3), .pin13(dipswitch_2_sw8),
    .pin12(dipswitch_2_sw8), .pin11(n7400_2_pin1), .pin10(dipswitch_2_sw7), .pin9(dipswitch_2_sw7),
    .pin8(n7400_2_pin2));  // open: pin4, pin5, pin6
  LED led_5 (.in(n7400_1_pin8));
  LED led_6 (.in(n7400_2_pin3));

  // Notes on the sheet:
  //   A
  //   C
  //   D
  //   E
  //   F
  //   NOT Gate using NAND
  //   (CD)'
  //   AND Gate using NAND
  //   E'
  //   F'
  //   OR GATE using NAND
  //   A'
  //   CD
  //   E+F
  //   NOT
  //   OR
  //   AND
endmodule
