// Logisim project Universality_of_NOR_GATE.circ as structural Verilog: 1 circuit, main circuit main
module main (
);

  wire dipswitch_1_sw1, dipswitch_1_sw4, dipswitch_1_sw5, dipswitch_1_sw7, dipswitch_1_sw8, dipswitch_2_sw1,
       dipswitch_2_sw3, dipswitch_2_sw4, dipswitch_2_sw6, dipswitch_2_sw7, n7402_1_pin1, n7402_1_pin4,
       n7402_1_pin10, n7402_2_pin4, n7402_2_pin5, n7402_2_pin6, nor_1_out, nor_2_out, nor_3_out, nor_4_out,
       nor_5_out, nor_6_out;

  DipSwitch dipswitch_1 (
    .sw1(dipswitch_1_sw1), .sw4(dipswitch_1_sw4), .sw5(dipswitch_1_sw5), .sw7(dipswitch_1_sw7),
    .sw8(dipswitch_1_sw8));  // open: sw2, sw3, sw6
  nor nor_1 (nor_1_out, dipswitch_1_sw1, dipswitch_1_sw1);
  nor nor_2 (nor_2_out, dipswitch_1_sw4, dipswitch_1_sw5);
  nor nor_3 (nor_3_out, dipswitch_1_sw7, dipswitch_1_sw7);
  nor nor_4 (nor_4_out, dipswitch_1_sw8, dipswitch_1_sw8);
  LED led_1 (.in(nor_1_out));
  nor nor_5 (nor_5_out, nor_2_out, nor_2_out);
  nor nor_6 (nor_6_out, nor_3_out, nor_4_out);
  LED led_2 (.in(nor_5_out));
  LED led_3 (.in(nor_6_out));
  LED led_4 (.in(n7402_1_pin1));
  DipSwitch dipswitch_2 (
    .sw1(dipswitch_2_sw1), .sw3(dipswitch_2_sw3), .sw4(dipswitch_2_sw4), .sw6(dipswitch_2_sw6),
    .sw7(dipswitch_2_sw7));  // open: sw2, sw5, sw8
  _7402 u_7402_1 (
    .pin1(n7402_1_pin1), .pin2(dipswitch_2_sw1), .pin3(dipswitch_2_sw1), .pin4(n7402_1_pin4),
    .pin5(dipswitch_2_sw3), .pin6(dipswitch_2_sw4), .pin10(n7402_1_pin10), .pin9(n7402_1_pin4),
    .pin8(n7402_1_pin4));  // open: pin13, pin12, pin11
  _7402 u_7402_2 (
    .pin4(n7402_2_pin4), .pin5(n7402_2_pin5), .pin6(n7402_2_pin6), .pin13(n7402_2_pin5),
    .pin12(dipswitch_2_sw7), .pin11(dipswitch_2_sw7), .pin10(n7402_2_pin6), .pin9(dipswitch_2_sw6),
    .pin8(dipswitch_2_sw6));  // open: pin1, pin2, pin3
  LED led_5 (.in(n7402_1_pin10));
  LED led_6 (.in(n7402_2_pin4));

  // Notes on the sheet:
  //   A
  //   C
  //   D
  //   E
  //   F
  //   NOT Gate using NOR
  //   (C+D)'
  //   OR Gate using NOR
  //   E'
  //   F'
  //   AND GATE using NOR
  //   A'
  //   C+D
  //   EF
  //   NOT
  //   OR
  //   AND
endmodule
