// Logisim project XNOR_GATE_74266.circ as structural Verilog: 1 circuit, main circuit main
// A
module main (
  input  C,
  input  D
);

  wire dipswitch_1_sw1, dipswitch_1_sw8, n747266_1_p4, xnor_1_out;

  DipSwitch dipswitch_1 (.sw1(dipswitch_1_sw1), .sw8(dipswitch_1_sw8));  // open: sw2, sw3, sw4, sw5, sw6, sw7
  // _747266 747266_1: pin names not known; wires that end beside it: 1'b1, dipswitch_1_sw1, dipswitch_1_sw8, n747266_1_p4, 1'b0
  LED Y (.in(n747266_1_p4));
  xnor xnor_1 (xnor_1_out, C, D);
  LED X (.in(xnor_1_out));

  // Notes on the sheet:
  //   A
  //   Inputs
  //   B
  //   Output LED
endmodule
