// Logisim project XOR_GATE_7486.circ as structural Verilog: 1 circuit, main circuit main
// A
module main (
  input  C,
  input  D
);

  wire dipswitch_1_sw1, dipswitch_1_sw8, n7486_1_p4, xor_1_out;

  DipSwitch dipswitch_1 (.sw1(dipswitch_1_sw1), .sw8(dipswitch_1_sw8));  // open: sw2, sw3, sw4, sw5, sw6, sw7
  // _7486 7486_1: pin names not known; wires that end beside it: 1'b1, dipswitch_1_sw1, dipswitch_1_sw8, n7486_1_p4, 1'b0
  LED Y (.in(n7486_1_p4));
  xor xor_1 (xor_1_out, C, D);
  LED X (.in(xor_1_out));

  // Notes on the sheet:
  //   A
  //   B
  //   Inputs
  //   Output LED
endmodule
