// Logisim project subtractor.circ as structural Verilog: 1 circuit, main circuit main
module main (
  input  A,
  input  B,
  input  C
);

  wire and_1_out, and_2_out, n7404_1_pin2, n7404_1_pin4, n7408_1_pin3, n7408_1_pin6, n7432_1_p4,
       n7486_1_pin1, n7486_1_pin2, n7486_1_pin3, n7486_1_pin5, n7486_1_pin6, not_1_out, not_2_out, or_1_out,
       xor_1_out, xor_2_out;

  _7486 u_7486_1 (
    .pin1(n7486_1_pin1), .pin2(n7486_1_pin2), .pin3(n7486_1_pin3), .pin4(n7486_1_pin3), .pin5(n7486_1_pin5),
    .pin6(n7486_1_pin6));  // open: pin13, pin12, pin11, pin10, pin9, pin8
  DipSwitch dipswitch_1 (.sw1(n7486_1_pin1), .sw2(n7486_1_pin2), .sw3(n7486_1_pin5));  // open: sw4, sw5, sw6, sw7, sw8
  not not_1 (not_1_out, A);
  xor xor_1 (xor_1_out, A, B);
  and and_1 (and_1_out, B, not_1_out);
  _7404 u_7404_1 (
    .pin1(n7486_1_pin1), .pin2(n7404_1_pin2), .pin3(n7486_1_pin3), .pin4(n7404_1_pin4));  // open: pin5, pin6, pin13, pin12, pin11, pin10, pin9, pin8
  LED led_1 (.in(xor_1_out));
  LED led_2 (.in(and_1_out));
  not not_2 (not_2_out, xor_1_out);
  _7408 u_7408_1 (
    .pin1(n7486_1_pin2), .pin2(n7404_1_pin2), .pin3(n7408_1_pin3), .pin4(n7404_1_pin4), .pin5(n7486_1_pin5),
    .pin6(n7408_1_pin6));  // open: pin13, pin12, pin11, pin10, pin9, pin8
  and and_2 (and_2_out, not_2_out, C);
  xor xor_2 (xor_2_out, xor_1_out, C);
  // _7432 7432_1: pin names not known; wires that end beside it: 1'b1, n7408_1_pin6, n7408_1_pin3, n7432_1_p4, 1'b0
  or or_1 (or_1_out, and_2_out, and_1_out);
  LED led_3 (.in(xor_2_out));
  LED led_4 (.in(or_1_out));
  LED led_5 (.in(n7486_1_pin3));
  LED led_6 (.in(n7408_1_pin3));
  LED led_7 (.in(n7486_1_pin6));
  LED led_8 (.in(n7432_1_p4));

  // Notes on the sheet:
  //   B
  //   A'
  //   A'B+AB'
  //   Half Subtractor, Difference
  //   Half Subtractor, Borrow
  //   A'B+AB'
  //   C
  //   C(A'B+AB')'
  //   A'B
  //   C(A'B+AB')+C'(AB+A'B')
  //   C(A'B+AB')'+A'B
  //   Full Subtractor, Difference
  //   Full Subtractor, Borrow
  //   Half Subtractor, Difference
  //   Half Subtractor, Borrow
  //   Full Subtractor, Difference
  //   Full Subtractor, Borrow
endmodule
