// Logisim project Implementation_of_Boolean_function_using_MUX.circ as structural Verilog: 1 circuit, main circuit main
module main (
  input  _0,
  input  _1,
  input  in_3
);

  wire dipswitch_1_sw1, dipswitch_1_sw2, dipswitch_1_sw3, dipswitch_1_sw8, n7404_1_p3, n74151_1_pin5;

  DipSwitch dipswitch_1 (
    .sw1(dipswitch_1_sw1), .sw2(dipswitch_1_sw2), .sw3(dipswitch_1_sw3), .sw8(dipswitch_1_sw8));  // open: sw4, sw5, sw6, sw7
  // _7404 7404_1: pin names not known; wires that end beside it: 1'b1, dipswitch_1_sw8, n7404_1_p3, 1'b0
  _74151 u_74151_1 (
    .pin1(n7404_1_p3), .pin2(_0), .pin3(_1), .pin4(_1), .pin5(n74151_1_pin5), .pin7(in_3),
    .pin15(n7404_1_p3), .pin14(_0), .pin13(_0), .pin12(dipswitch_1_sw8), .pin11(dipswitch_1_sw3),
    .pin10(dipswitch_1_sw2), .pin9(dipswitch_1_sw1));  // open: pin6
  LED led_1 (.in(n74151_1_pin5));

  // Notes on the sheet:
  //   A'
  //   A
  //   A'
  //   0
  //   A
  //   A'
  //   1
  //   0
  //   S2
  //   S1
  //   S0
  //   0
  //   F
endmodule
