// Logisim project Implementation_of_Boolean_function_using_MUX_with_gates.circ as structural Verilog: 1 circuit, main circuit main
module main (
  input  _1,
  input  _0,
  input  E_prime
);

  wire and_1_out, and_2_out, and_3_out, and_4_out, and_5_out, and_6_out, and_7_out, and_8_out,
       dipswitch_1_sw1, dipswitch_1_sw2, dipswitch_1_sw3, dipswitch_1_sw8, not_1_out, not_2_out, not_3_out,
       not_4_out, not_5_out, not_6_out, or_1_out, or_2_out, or_3_out, or_4_out, or_5_out, or_6_out, or_7_out;

  DipSwitch dipswitch_1 (
    .sw1(dipswitch_1_sw1), .sw2(dipswitch_1_sw2), .sw3(dipswitch_1_sw3), .sw8(dipswitch_1_sw8));  // open: sw4, sw5, sw6, sw7
  not not_1 (not_1_out, dipswitch_1_sw8);
  not not_2 (not_2_out, dipswitch_1_sw3);
  not not_3 (not_3_out, dipswitch_1_sw2);
  not not_4 (not_4_out, dipswitch_1_sw1);
  not not_5 (not_5_out, E_prime);
  and and_1 (and_1_out, _1, not_4_out, not_3_out, not_2_out, not_5_out);
  and and_2 (and_2_out, _1, not_4_out, not_3_out, dipswitch_1_sw3, not_5_out);
  and and_3 (and_3_out, _0, not_4_out, dipswitch_1_sw2, not_2_out, not_5_out);
  and and_4 (and_4_out, not_1_out, not_4_out, dipswitch_1_sw2, dipswitch_1_sw3, not_5_out);
  and and_5 (and_5_out, not_1_out, dipswitch_1_sw1, not_3_out, not_2_out, not_5_out);
  and and_6 (and_6_out, _0, dipswitch_1_sw1, not_3_out, dipswitch_1_sw3, not_5_out);
  and and_7 (and_7_out, _0, dipswitch_1_sw1, dipswitch_1_sw2, not_2_out, not_5_out);
  and and_8 (and_8_out, dipswitch_1_sw8, dipswitch_1_sw1, dipswitch_1_sw2, dipswitch_1_sw3, not_5_out);
  or or_1 (or_1_out, and_1_out, and_2_out);
  or or_2 (or_2_out, and_7_out, and_8_out);
  or or_3 (or_3_out, and_3_out, and_4_out);
  or or_4 (or_4_out, and_5_out, and_6_out);
  or or_5 (or_5_out, or_1_out, or_3_out);
  or or_6 (or_6_out, or_4_out, or_2_out);
  not not_6 (not_6_out, or_7_out);
  LED led_1 (.in(not_6_out));
  or or_7 (or_7_out, or_5_out, or_6_out);
  LED led_2 (.in(or_7_out));

  // Notes on the sheet:
  //   A'
  //   A
  //   1
  //   S0
  //   S1
  //   S2
  //   0
  //   0
  //   I0
  //   I1
  //   S0'
  //   I2
  //   S1'
  //   I3
  //   A'
  //   I4
  //   S2'
  //   I5
  //   I6
  //   I7
  //   A
  //   0
  //   A'
  //   E
  //   S0'S1'S2'I0
  //   S0S1'S2'I1
  //   S0'S1S2'I2
  //   S0S1S2'I3
  //   S0'S1'S2I4
  //   S0S1'S2I5
  //   S0'S1S2I6
  //   S0S1S2I7
  //   F'
  //   F
endmodule
