// Logisim project priority_encoder_4to2.circ as structural Verilog: 1 circuit, main circuit main
module main (
  input  D3,
  input  D2,
  input  D1,
  input  D0
);

  wire and_1_out, dipswitch_1_sw1, dipswitch_1_sw5, dipswitch_1_sw8, n7404_1_p2, n7404_1_p3, n7432_1_pin2,
       n7432_1_pin3, n7432_1_pin6, n7432_1_pin11, n7432_1_pin12, not_1_out, or_1_out, or_2_out, or_3_out,
       or_4_out;

  // _7404 7404_1: pin names not known; wires that end beside it: 1'b1, n7404_1_p2, n7404_1_p3, 1'b0
  DipSwitch dipswitch_1 (
    .sw1(dipswitch_1_sw1), .sw3(n7404_1_p2), .sw5(dipswitch_1_sw5), .sw8(dipswitch_1_sw8));  // open: sw2, sw4, sw6, sw7
  not not_1 (not_1_out, D2);
  or or_1 (or_1_out, D3, D2);
  _7432 u_7432_1 (
    .pin1(dipswitch_1_sw1), .pin2(n7432_1_pin2), .pin3(n7432_1_pin3), .pin4(dipswitch_1_sw1),
    .pin5(n7404_1_p2), .pin6(n7432_1_pin6), .pin13(dipswitch_1_sw8), .pin12(n7432_1_pin12),
    .pin11(n7432_1_pin11), .pin10(dipswitch_1_sw5), .pin9(n7432_1_pin6), .pin8(n7432_1_pin12));
  or or_2 (or_2_out, or_1_out, D1);
  and and_1 (and_1_out, not_1_out, D1);
  // _7408 7408_1: pin names not known; wires that end beside it: 1'b1, n7404_1_p3, dipswitch_1_sw5, n7432_1_pin2, 1'b0
  or or_3 (or_3_out, or_2_out, D0);
  or or_4 (or_4_out, D3, and_1_out);
  LED led_1 (.in(or_4_out));
  LED led_2 (.in(or_1_out));
  LED led_3 (.in(or_3_out));
  LED led_4 (.in(n7432_1_pin6));
  LED led_5 (.in(n7432_1_pin3));
  LED led_6 (.in(n7432_1_pin11));

  // Notes on the sheet:
  //   D3
  //   D2
  //   D3 D2 D1 D0
  //   D2+D3
  //   D1
  //   D2'
  //   D1
  //   D1D2'
  //   D1+D2+D3
  //   D3
  //   y  =D3+D1D2'
  //   x = D2+D3
  //   x
  //   y
  //   V
  //   V = D0+D1+D2+D3
endmodule
