// Logisim project jk_ff_using_block.circ as structural Verilog: 1 circuit, main circuit main
module main (
  input  J,
  input  Set,
  input  K,
  input  Reset
);

  wire CLK_out, j_k_ff_1_q, j_k_ff_1_qn;

  Clock CLK (.out(CLK_out));
  J_K_Flip_Flop j_k_ff_1 (.J(J), .K(K), .clk(CLK_out), .Q(j_k_ff_1_q), .Qn(j_k_ff_1_qn), .preset(Set), .reset(Reset));
  LED Q (.in(j_k_ff_1_q));
  LED led_1 (.in(j_k_ff_1_qn));

  // Notes on the sheet:
  //   Q'
endmodule
