// Logisim project jk_ff_using_gates.circ as structural Verilog: 1 circuit, main circuit main
module main (
  input  Pr,
  input  J,
  input  K,
  input  Cr
);

  wire CLK_out, nand_1_out, nand_2_out, nand_3_out, nand_4_out, nand_5_out, nand_6_out, nand_7_out,
       nand_8_out, not_1_out;

  Clock CLK (.out(CLK_out));
  nand nand_1 (nand_1_out, nand_8_out, J, CLK_out);
  nand nand_2 (nand_2_out, CLK_out, K, nand_7_out);
  nand nand_3 (nand_3_out, Pr, nand_1_out, nand_4_out);
  nand nand_4 (nand_4_out, nand_3_out, nand_2_out, Cr);
  not not_1 (not_1_out, CLK_out);
  nand nand_5 (nand_5_out, nand_3_out, not_1_out);
  nand nand_6 (nand_6_out, not_1_out, nand_4_out);
  nand nand_7 (nand_7_out, nand_5_out, nand_8_out);
  nand nand_8 (nand_8_out, nand_7_out, nand_6_out);
  LED led_1 (.in(nand_7_out));
  LED led_2 (.in(nand_8_out));

  // Notes on the sheet:
  //   Q'
  //   Q
  //   Master
  //   Qm
  //   Qm'
  //   CLK'
  //   Slave
  //   Q
  //   Q'
endmodule
