// Logisim project AND_GATE_7408.circ as structural Verilog: 1 circuit, main circuit main
// A
module main (
  input  C,
  input  D
);

  wire and_1_out, dipswitch_1_sw1, dipswitch_1_sw7, n7408_1_p4;

  DipSwitch dipswitch_1 (.sw1(dipswitch_1_sw1), .sw7(dipswitch_1_sw7));  // open: sw2, sw3, sw4, sw5, sw6, sw8
  // _7408 7408_1: pin names not known; wires that end beside it: 1'b1, dipswitch_1_sw1, dipswitch_1_sw7, n7408_1_p4, 1'b0
  LED Y (.in(n7408_1_p4));
  and and_1 (and_1_out, C, D);
  LED X (.in(and_1_out));

  // Notes on the sheet:
  //   A
  //   B
  //   Inputs
  //   Output LED
endmodule
