// Logisim project NOR_GATE_7402.circ as structural Verilog: 1 circuit, main circuit main
// A
module main (
  input  C,
  input  in_2
);

  wire dipswitch_1_sw1, dipswitch_1_sw8, nor_1_out, nor_gate_p2;

  DipSwitch dipswitch_1 (.sw1(dipswitch_1_sw1), .sw8(dipswitch_1_sw8));  // open: sw2, sw3, sw4, sw5, sw6, sw7
  LED led_1 (.in(nor_gate_p2));
  // _7402 nor_gate: pin names not known; wires that end beside it: 1'b1, nor_gate_p2, dipswitch_1_sw1, dipswitch_1_sw8, 1'b0
  nor nor_1 (nor_1_out, C, in_2);
  LED X (.in(nor_1_out));

  // Notes on the sheet:
  //   A
  //   Inputs
  //   X
  //   B
  //   Output LED
endmodule
