// Logisim project NOT_GATE_7404.circ as structural Verilog: 1 circuit, main circuit main
// A
module main (
  input  C
);

  wire dipswitch_1_sw1, n7404_1_p3, not_1_out;

  DipSwitch dipswitch_1 (.sw1(dipswitch_1_sw1));  // open: sw2, sw3, sw4, sw5, sw6, sw7, sw8
  // _7404 7404_1: pin names not known; wires that end beside it: 1'b1, dipswitch_1_sw1, n7404_1_p3, 1'b0
  LED Y (.in(n7404_1_p3));
  not not_1 (not_1_out, C);
  LED X (.in(not_1_out));

  // Notes on the sheet:
  //   A
  //   Input
  //   Output LED
endmodule
