// Logisim project OR_GATE_7432.circ as structural Verilog: 1 circuit, main circuit main
// A
module main (
  input  C,
  input  D
);

  wire dipswitch_1_sw1, dipswitch_1_sw7, n7432_1_p4, or_1_out;

  DipSwitch dipswitch_1 (.sw1(dipswitch_1_sw1), .sw7(dipswitch_1_sw7));  // open: sw2, sw3, sw4, sw5, sw6, sw8
  // _7432 7432_1: pin names not known; wires that end beside it: 1'b1, dipswitch_1_sw1, dipswitch_1_sw7, n7432_1_p4, 1'b0
  LED Y (.in(n7432_1_p4));
  or or_1 (or_1_out, C, D);
  LED X (.in(or_1_out));

  // Notes on the sheet:
  //   A
  //   B
  //   Inputs
  //   Output LED
endmodule
