// Logisim project Implementation_of_4_bit_asynchronous_up_counter.circ as structural Verilog: 1 circuit, main circuit main
module main (
  input  in_1,
  input  in_2
);

  wire CLK_out, j_k_ff_1_q, j_k_ff_2_q, j_k_ff_3_q, j_k_ff_4_q;

  Clock CLK (.out(CLK_out));
  J_K_Flip_Flop #(.trigger("falling")) j_k_ff_1 (
    .J(in_1), .K(in_1), .clk(CLK_out), .Q(j_k_ff_1_q), .preset(in_2), .reset(in_2));  // open: Qn
  J_K_Flip_Flop #(.trigger("falling")) j_k_ff_2 (
    .J(in_1), .K(in_1), .clk(j_k_ff_1_q), .Q(j_k_ff_2_q), .preset(in_2), .reset(in_2));  // open: Qn
  J_K_Flip_Flop #(.trigger("falling")) j_k_ff_3 (
    .J(in_1), .K(in_1), .clk(j_k_ff_2_q), .Q(j_k_ff_3_q), .preset(in_2), .reset(in_2));  // open: Qn
  LED led_1 (.in(j_k_ff_4_q));
  LED led_2 (.in(j_k_ff_3_q));
  LED led_3 (.in(j_k_ff_2_q));
  LED led_4 (.in(j_k_ff_1_q));
  J_K_Flip_Flop #(.trigger("falling")) j_k_ff_4 (
    .J(in_1), .K(in_1), .clk(j_k_ff_3_q), .Q(j_k_ff_4_q), .preset(in_2), .reset(in_2));  // open: Qn

  // Notes on the sheet:
  //   Logic HIGH
  //   MSB          LSB
endmodule
